# Fritzing sketch fritzing-audio (saved by Fritzing 0.9.6b)
breadboards: 1

parts:
  M1 = DOIT Esp32 DevKit v1 (30 pins long, 11 pins width) [part_number=ESP32S-PIN30]
  BAT1 = Battery Holders [package=battery-aa-kit]
  BAT2 = Battery Holders [package=battery-aa-kit]
  BAT3 = Battery Holders [package=battery-aa-kit]
  BAT4 = Battery Holders [package=battery-aa-kit]
  S1 = SPST Switch [package=switch-spdt]
  SP1 = SPEAKER [package=pcb_mount_speaker]
  Part1 = Adafruit MAX98357A I2S 3W Class D Amplifier [part_number="Adafruit #3006"]

nets:
  N1: M1.GND, S1.O
  N2: M1.D18, Part1.LRCLK
  N3: M1.D19, Part1.BCLK
  N4: M1.D21, Part1.DIN
  VIN: M1.VIN, BAT1.-, BAT2.+, Part1.VIN, Part1.GND, Part1.GAIN
  N5: BAT2.-, BAT3.+
  N6: BAT3.-, BAT4.+
  N7: BAT4.-, S1.P
  N8: SP1.+, Part1.VO-
  N9: SP1.-, Part1.VO+

custom parts:
  DOIT Esp32 DevKit v1 (30 pins long, 11 pins width): The DOIT Esp32 DevKit v1 is one of the development board created by DOIT to evaluate the ESP-WROOM-32 module. It is based on the ESP32 microcontroller that boasts Wifi, Bluetooth, Ethernet and Low Power support all in a single chip. (vanepp) made breadboard work, adjusted pin numbering and labels and reduced size of schematic and cleaned up pcb. This chip is 30pins long (2 x15) and 11 pins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
  Adafruit MAX98357A I2S 3W Class D Amplifier: Listen to this good news - we now have an all in one digital audio amp breakout board that works incredibly well with the Raspberry Pi! If you're looking for an easy and low cost way to get you digital sound files bumpin' then the MAX08357 I2S Amp Breakout is for you. It takes standard I2S digital audio input and, not only decodes it into analog, but also amplifies it directly into a speaker.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
