# Fritzing sketch legoturtle (saved by Fritzing 0.8.7b)
breadboards: 1

parts:
  Board_1 = Arduino Leonardo (Rev3b)
  S1_(Left) = Pushbutton [package=THT]
  S2_(Right) = Pushbutton [package=THT]
  M2_(Right) = DC Motor
  M1_(Left) = DC Motor
  IC2 = H-Bridge [part_number=SN754410NE package=THT]
  R2 = Resistor [tolerance=±5% resistance=100k package=THT]
  R1 = Resistor [tolerance=±5% resistance=100k package=THT]

nets:
  N1: Board_1.D2/SDA, S1_(Left).leg1, R1.Pin_0
  N2: Board_1.D3_PWM/SCL, S2_(Right).leg1, R2.Pin_0
  N3: Board_1.5V, S1_(Left).leg0, S2_(Right).leg0, IC2.1_2EN, IC2.3_4EN, IC2.VCC1
  GND: Board_1.GND, IC2.GND1, IC2.GND2, IC2.GND3, IC2.GND4, R2.Pin_1, R1.Pin_1
  N4: Board_1.VIN, IC2.VCC2
  N5: Board_1.D9_PWM/A9, IC2.1A
  N6: Board_1.D10_PWM/A10, IC2.2A
  N7: Board_1.D11_PWM, IC2.3A
  N8: Board_1.D12/A11, IC2.4A
  N9: M2_(Right).pin_1, IC2.4Y
  N10: M2_(Right).pin_2, IC2.3Y
  N11: M1_(Left).pin_1, IC2.2Y
  N12: M1_(Left).pin_2, IC2.1Y
